# Fritzing sketch gps-backtrack (saved by Fritzing 0.9.3b)
stripboards: 1

parts:
  Part1 = adafruit [part_number="Adafruit #2000"]
  S1 = Momentary Switch [package=ksa_sealed_tac_switch]
  S2 = Momentary Switch [package=ksa_sealed_tac_switch]
  S3 = Toggle Switch [package=THT]
  S4 = Toggle Switch [package=THT]
  OLED_I2C1 = OLED 128x64 I2C Monochrome Display
  U1 = SUP500F [package=sup500f]
  VCC1 = Battery

nets:
  GND: Part1.connector72, S1.1, S1.2, S2.1, S2.2, OLED_I2C1.GND, U1.GND, VCC1.-
  VDD: Part1.connector74, S3.L2, OLED_I2C1.VDD, U1.VCC
  N1: Part1.connector78, S2.3, S2.4
  N2: Part1.connector79, S1.3, S1.4
  N3: Part1.connector81, S4.L2
  N4: Part1.connector95, OLED_I2C1.SDA
  N5: Part1.connector96, OLED_I2C1.SCK
  N6: S3.COM, VCC1.+
  N7: S4.COM, U1.TX-O

notes:
  purple: OLED SCL <-> Pro SCL
  orange: OLED SDA <-> Pro SDA
  blue: screen btn <-> Pro 3
  yellow: save btn <-> Pro 4
  white: GPS TX <-> Pro RX (switched)
